// Logisim project 8 bit MIPS.circ as structural Verilog: 4 circuits, main circuit main
module main (
  output [7:0] A,
  output [7:0] B,
  output [7:0] F
);

  wire alu_1_zf, and_1_out, and_2_out, clock_1_out, control_unit_1_alusrc1, control_unit_1_branch_equal,
       control_unit_1_branch_not_equal, control_unit_1_jump, control_unit_1_memread, control_unit_1_memtoreg,
       control_unit_1_memwrite, control_unit_1_regdst, control_unit_1_regwrite, not_1_out, or_1_out;
  wire [1:0] control_unit_1_alusrc2;
  wire [2:0] control_unit_1_aluop;
  wire [3:0] multiplexer_1_out;
  wire [7:0] adder_1_out, adder_2_out, multiplexer_4_out, multiplexer_5_out, multiplexer_6_out, PC_q,
       ram_1_data, register_file_1_readdata1, register_file_1_readdata2;
  wire [19:0] rom_1_data;

  Clock clock_1 (.out(clock_1_out));
  Register #(.trigger("falling")) PC (.D(multiplexer_6_out), .Q(PC_q), .clk(clock_1_out));  // open: en, clr
  Adder adder_1 (.a(PC_q), .b(8'h1), .out(adder_1_out), .cin(1'b0));  // open: cout
  ROM #(.dataWidth(20)) rom_1 (.addr(PC_q), .data(rom_1_data));  // open: sel
  Control_Unit control_unit_1 (
    .Opcode(rom_1_data[19:16]), .RegWrite(control_unit_1_regwrite), .MemRead(control_unit_1_memread),
    .MemWrite(control_unit_1_memwrite), .MemtoReg(control_unit_1_memtoreg), .RegDst(control_unit_1_regdst),
    .ALUSrc1(control_unit_1_alusrc1), .ALUSrc2(control_unit_1_alusrc2), .ALUop(control_unit_1_aluop),
    .branch_equal(control_unit_1_branch_equal), .branch_not_equal(control_unit_1_branch_not_equal),
    .jump(control_unit_1_jump));
  Multiplexer #(.width(4), .enable("false")) multiplexer_1 (
    .in0(rom_1_data[11:8]), .in1(rom_1_data[7:4]), .out(multiplexer_1_out), .sel(control_unit_1_regdst));
  Register_File register_file_1 (
    .WriteData(multiplexer_4_out), .ReadRegister1(rom_1_data[15:12]), .RegWrite(control_unit_1_regwrite),
    .WriteRegister(multiplexer_1_out), .ReadRegister2(rom_1_data[11:8]), .Clk(clock_1_out),
    .ReadData1(register_file_1_readdata1), .ReadData2(register_file_1_readdata2));
  Adder adder_2 (.a(adder_1_out), .b(rom_1_data[7:0]), .out(adder_2_out), .cin(1'b0));  // open: cout
  Multiplexer #(.width(8), .enable("false")) multiplexer_2 (
    .in0(register_file_1_readdata1), .in1(register_file_1_readdata2), .out(A), .sel(control_unit_1_alusrc1));
  Multiplexer #(.select(2), .width(8), .enable("false")) multiplexer_3 (
    .in0(register_file_1_readdata2), .in1({4'b0000, rom_1_data[3:0]}), .in2(rom_1_data[7:0]),
    .in3({8{1'b0}}), .out(B), .sel(control_unit_1_alusrc2));
  ALU alu_1 (.A(A), .B(B), .ALUop(control_unit_1_aluop), .ZF(alu_1_zf), .F(F));
  Multiplexer #(.width(8), .enable("false")) multiplexer_4 (
    .in0(F), .in1(ram_1_data), .out(multiplexer_4_out), .sel(control_unit_1_memtoreg));
  Multiplexer #(.width(8), .enable("false")) multiplexer_5 (
    .in0(adder_1_out), .in1(adder_2_out), .out(multiplexer_5_out), .sel(or_1_out));
  or or_1 (or_1_out, and_1_out, and_2_out);
  and and_1 (and_1_out, alu_1_zf, control_unit_1_branch_equal);
  and and_2 (and_2_out, not_1_out, control_unit_1_branch_not_equal);
  not not_1 (not_1_out, alu_1_zf);
  Multiplexer #(.width(8), .enable("false")) multiplexer_6 (
    .in0(multiplexer_5_out), .in1(rom_1_data[15:8]), .out(multiplexer_6_out), .sel(control_unit_1_jump));
  RAM #(.bus("separate")) ram_1 (
    .addr(F), .din(register_file_1_readdata2), .data(ram_1_data), .str(control_unit_1_memwrite), .sel(1'b1),
    .clk(clock_1_out), .ld(control_unit_1_memread));  // open: clr

  // Notes on the sheet:
  //   Instruction Memory
  //   contents of rom_1 (hex, n*v repeats v):
  //   50000 706ff 7020a 70305 42310 41340 44150 c3203 30221 d4201 b1f00 25150 a2202 80441 f3203 62410 1530
  //   b1e00 c6100 a6601 c6300 a6601 11105 76601 f6100 53314 76601 f6300 93330 b1f00 e31f3
  //   Control_Unit
  //   Registers_File
  //   ALU
  //   Data Memory
endmodule

module ALU (
  input  [7:0] A,
  input  [7:0] B,
  input  [2:0] ALUop,
  output ZF,
  output [7:0] F
);

  wire [7:0] adder_1_out, and_1_out, nor_1_out, or_1_out, subtractor_1_out;
  wire [15:0] shifter_1_out, shifter_2_out;

  Adder adder_1 (.a(A), .b(B), .out(adder_1_out), .cin(1'b0));  // open: cout
  Subtractor subtractor_1 (.a(A), .b(B), .out(subtractor_1_out), .bin(1'b0));  // open: bout
  assign or_1_out = A | B;  // OR_Gate or_1, 8 bits wide
  assign and_1_out = A & B;  // AND_Gate and_1, 8 bits wide
  assign nor_1_out = ~(A | B);  // NOR_Gate nor_1, 8 bits wide
  Shifter #(.width(16)) shifter_1 (.in({{8{1'b0}}, A}), .\dist (B[3:0]), .out(shifter_1_out));
  Shifter #(.width(16), .shift("lr")) shifter_2 (.in({{8{1'b0}}, A}), .\dist (B[3:0]), .out(shifter_2_out));
  Multiplexer #(.select(3), .width(8), .enable("false")) multiplexer_1 (
    .in0(adder_1_out), .in1(subtractor_1_out), .in2(or_1_out), .in3(and_1_out), .in4(nor_1_out),
    .in5(shifter_1_out[7:0]), .in6(shifter_2_out[7:0]), .in7({8{1'b0}}), .out(F), .sel(ALUop));
  nor nor_2 (ZF, F[0], F[1], F[2], F[3], F[4], F[5], F[6], F[7]);
endmodule

module Register_File (
  input  [7:0] WriteData,
  input  [3:0] ReadRegister1,
  input  RegWrite,
  input  [3:0] WriteRegister,
  input  Clk,
  input  [3:0] ReadRegister2,
  output [7:0] ReadData1,
  output [7:0] ReadData2
);

  wire decoder_1_out0, decoder_1_out1, decoder_1_out2, decoder_1_out3, decoder_1_out4, decoder_1_out5,
       decoder_1_out6, decoder_1_out7;
  wire [7:0] sp_q, t0_q, t1_q, t2_q, t3_q, t4_q, zero_q;

  Decoder #(.select(3), .disabled(0)) decoder_1 (
    .out0(decoder_1_out0), .out1(decoder_1_out1), .out2(decoder_1_out2), .out3(decoder_1_out3),
    .out4(decoder_1_out4), .out5(decoder_1_out5), .out6(decoder_1_out6), .out7(decoder_1_out7),
    .sel(WriteRegister[2:0]), .en(RegWrite));
  Register #(.trigger("falling")) zero (.D(WriteData), .en(decoder_1_out0), .Q(zero_q), .clk(Clk));  // open: clr
  Register #(.trigger("falling")) t0 (.D(WriteData), .en(decoder_1_out1), .Q(t0_q), .clk(Clk));  // open: clr
  Register #(.trigger("falling")) t1 (.D(WriteData), .en(decoder_1_out2), .Q(t1_q), .clk(Clk));  // open: clr
  Register #(.trigger("falling")) t2 (.D(WriteData), .en(decoder_1_out3), .Q(t2_q), .clk(Clk));  // open: clr
  Register #(.trigger("falling")) t3 (.D(WriteData), .en(decoder_1_out4), .Q(t3_q), .clk(Clk));  // open: clr
  Register #(.trigger("falling")) t4 (.D(WriteData), .en(decoder_1_out5), .Q(t4_q), .clk(Clk));  // open: clr
  Register #(.trigger("falling")) sp (.D(WriteData), .en(decoder_1_out6), .Q(sp_q), .clk(Clk));  // open: clr
  Multiplexer #(.select(3), .width(8), .enable("false")) multiplexer_1 (
    .in0(zero_q), .in1(t0_q), .in2(t1_q), .in3(t2_q), .in4(t3_q), .in5(t4_q), .in6(sp_q), .in7({8{1'b0}}),
    .out(ReadData1), .sel(ReadRegister1[2:0]));
  Multiplexer #(.select(3), .width(8), .enable("false")) multiplexer_2 (
    .in0(zero_q), .in1(t0_q), .in2(t1_q), .in3(t2_q), .in4(t3_q), .in5(t4_q), .in6(sp_q), .in7({8{1'b0}}),
    .out(ReadData2), .sel(ReadRegister2[2:0]));
endmodule

module Control_Unit (
  input  [3:0] Opcode,
  output RegWrite,
  output MemRead,
  output MemWrite,
  output MemtoReg,
  output RegDst,
  output ALUSrc1,
  output [1:0] ALUSrc2,
  output [2:0] ALUop,
  output branch_equal,
  output branch_not_equal,
  output jump
);

  wire [15:14] rom_1_data;

  ROM #(.addrWidth(4), .dataWidth(16)) rom_1 (
    .addr(Opcode),
    .data({rom_1_data, jump, branch_not_equal, branch_equal, ALUop, ALUSrc2, ALUSrc1, RegDst, MemtoReg, MemWrite, MemRead, RegWrite}));  // open: sel

  // Notes on the sheet:
  //   contents of rom_1 (hex, n*v repeats v):
  //   211 281 111 571 11 381 311 81 671 411 181 2700 84 900 1100 8b
endmodule
