// Logisim project 4 bit ALU.circ as structural Verilog: 2 circuits, main circuit main
module main (
  input  [2:0] Control,
  input  [3:0] A,
  input  [3:0] B,
  output [3:0] F,
  output [3:0] ZSCV
);

  wire n4_bit_alu_1_c3;

  _4_bit_ALU u_4_bit_alu_1 (
    .cs2(Control[2]), .cs1(Control[1]), .cs0(Control[0]), .A0(A[0]), .B0(B[0]), .A1(A[1]), .B1(B[1]),
    .A2(A[2]), .B2(B[2]), .A3(A[3]), .B3(B[3]), .F0(F[0]), .F1(F[1]), .F2(F[2]), .F3(F[3]),
    .C3(n4_bit_alu_1_c3), .Cout(ZSCV[1]));
  xor xor_1 (ZSCV[0], ZSCV[1], n4_bit_alu_1_c3);
  nor nor_1 (ZSCV[3], F[0], F[1], F[2], F[3]);

  assign ZSCV[2] = F[3];
endmodule

module _4_bit_ALU (
  input  cs2,
  input  cs1,
  input  cs0,
  input  A0,
  input  B0,
  input  A1,
  input  B1,
  input  A2,
  input  B2,
  input  A3,
  input  B3,
  output F0,
  output F1,
  output F2,
  output F3,
  output C3,
  output Cout
);

  wire adder_1_cout, adder_2_cout, adder_3_cout, adder_4_cout, and_1_out, and_2_out, and_3_out, and_4_out,
       and_5_out, and_6_out, and_7_out, and_8_out, and_9_out, and_10_out, and_11_out, not_1_out, or_1_out,
       or_2_out, or_3_out, or_4_out, or_5_out, xnor_1_out;

  xnor xnor_1 (xnor_1_out, cs1, cs0);
  not not_1 (not_1_out, cs1);
  or or_1 (or_1_out, not_1_out, cs0);
  or or_2 (or_2_out, or_1_out, B0);
  and and_1 (and_1_out, B0, xnor_1_out);
  or or_3 (or_3_out, or_1_out, B1);
  and and_2 (and_2_out, B1, xnor_1_out);
  or or_4 (or_4_out, or_1_out, B2);
  and and_3 (and_3_out, B2, xnor_1_out);
  or or_5 (or_5_out, or_1_out, B3);
  and and_4 (and_4_out, B3, xnor_1_out);
  and and_5 (and_5_out, A0, or_2_out);
  and and_6 (and_6_out, A1, or_3_out);
  and and_7 (and_7_out, A2, or_4_out);
  and and_8 (and_8_out, A3, or_5_out);
  and and_9 (and_9_out, cs2, not_1_out);
  Adder #(.width(1)) adder_1 (.a(and_5_out), .b(and_1_out), .out(F0), .cin(and_9_out), .cout(adder_1_cout));
  Adder #(.width(1)) adder_2 (.a(and_6_out), .b(and_2_out), .out(F1), .cin(and_10_out), .cout(adder_2_cout));
  Adder #(.width(1)) adder_3 (.a(and_7_out), .b(and_3_out), .out(F2), .cin(and_11_out), .cout(adder_3_cout));
  Adder #(.width(1)) adder_4 (.a(and_8_out), .b(and_4_out), .out(F3), .cin(C3), .cout(adder_4_cout));
  and and_10 (and_10_out, adder_1_cout, not_1_out);
  and and_11 (and_11_out, adder_2_cout, not_1_out);
  and and_12 (C3, adder_3_cout, not_1_out);
  and and_13 (Cout, adder_4_cout, not_1_out);
endmodule
