// Logisim project FP Adder v4.circ as structural Verilog: 7 circuits, main circuit main
module main (
  input  [15:0] Num_A,
  input  [15:0] Num_B,
  output Underflow,
  output Overflow,
  output [15:0] Sum
);

  FP_Adder fp_adder_1 (.Num_A(Num_A), .Num_B(Num_B), .Sum(Sum), .Underflow(Underflow), .Overflow(Overflow));
endmodule

module Negator (
  input  Subtract,
  input  [12:0] Significand_in,
  output [12:0] Significand_out
);

  wire [12:0] xor_1_out;

  assign xor_1_out = {13{Subtract}} ^ Significand_in;  // XOR_Gate xor_1, 13 bits wide
  Adder #(.width(13)) adder_1 (.a({13{1'b0}}), .b(xor_1_out), .out(Significand_out), .cin(Subtract));  // open: cout
endmodule

module Position_Finder (
  input  [12:0] Significand,
  output [3:0] Position__w_r_t__2nd_leftmost_bit,
  output _1_exists
);

  wire [3:0] bitfinder_1_index;

  BitFinder #(.width(13)) bitfinder_1 (
    .in({Significand[0], Significand[1], Significand[2], Significand[3], Significand[4], Significand[5], Significand[6], Significand[7], Significand[8], Significand[9], Significand[10], Significand[11], Significand[12]}),
    .index(bitfinder_1_index), .found(_1_exists));
  Subtractor #(.width(4)) subtractor_1 (
    .a(bitfinder_1_index), .b(4'b0000), .out(Position__w_r_t__2nd_leftmost_bit), .bin(1'b1));  // open: bout
endmodule

module Normalizer (
  input  [12:0] Significand_In,
  input  [3:0] Exponent_In,
  output Underflow,
  output Overflow,
  output [10:0] Fraction_Out,
  output [3:0] Exponent_Out
);

  wire comparator_2_gt, position_finder_1__1_exists;
  wire [3:0] position_finder_1_position__w_r_t__2nd_leftmost_bit;
  wire [4:0] subtractor_1_out;
  wire [4:4] and_1_out;
  wire [12:0] shifter_1_out, shifter_2_out;
  wire [12:11] multiplexer_2_out;

  Subtractor #(.width(5)) subtractor_1 (
    .a({1'b0, Exponent_In}), .b({and_1_out[4], position_finder_1_position__w_r_t__2nd_leftmost_bit}),
    .out(subtractor_1_out));  // open: bin, bout
  Multiplexer #(.width(4), .disabled(0), .enable("false")) multiplexer_1 (
    .in0(4'b0000), .in1(subtractor_1_out[3:0]), .out(Exponent_Out), .sel(position_finder_1__1_exists));
  Comparator_part #(.width(5)) comparator_1 (.a(subtractor_1_out), .b(5'b00001), .lt(Underflow));  // open: gt, eq
  Comparator_part #(.width(5)) comparator_2 (.a(subtractor_1_out), .b(5'b01110), .gt(comparator_2_gt));  // open: eq, lt
  and and_1 (and_1_out[4], position_finder_1_position__w_r_t__2nd_leftmost_bit[3], position_finder_1_position__w_r_t__2nd_leftmost_bit[2], position_finder_1_position__w_r_t__2nd_leftmost_bit[1], position_finder_1_position__w_r_t__2nd_leftmost_bit[0]);
  and and_2 (Overflow, comparator_2_gt, position_finder_1__1_exists);
  Position_Finder position_finder_1 (
    .Significand(Significand_In),
    .Position__w_r_t__2nd_leftmost_bit(position_finder_1_position__w_r_t__2nd_leftmost_bit),
    ._1_exists(position_finder_1__1_exists));
  Multiplexer #(.width(13), .disabled(0), .enable("false")) multiplexer_2 (
    .in0(shifter_1_out), .in1(shifter_2_out), .out({multiplexer_2_out, Fraction_Out}), .sel(and_1_out[4]));
  Shifter #(.width(13)) shifter_1 (
    .in(Significand_In), .\dist (position_finder_1_position__w_r_t__2nd_leftmost_bit), .out(shifter_1_out));
  Shifter #(.width(13), .shift("lr")) shifter_2 (.in(Significand_In), .\dist (4'b0001), .out(shifter_2_out));

  // Notes on the sheet:
  //   Splitter
  //   Splitter
  //   Subtractor
  //   Splitter
  //   Splitter
  //   Comparator
  //   Comparator
  //   Shifter
  //   Shifter
endmodule

module FP_Adder (
  input  [15:0] Num_A,
  input  [15:0] Num_B,
  output Underflow,
  output Overflow,
  output [15:0] Sum
);

  wire comparator_1_num_a___num_b, xor_1_out;
  wire [3:0] comparator_1_exponent_diff, multiplexer_2_out;
  wire [12:0] adder_1_out, extender_1_significand, extender_2_significand, multiplexer_3_out,
       multiplexer_4_out, negator_1_significand_out, shifter_1_out;

  Multiplexer #(.disabled(0), .enable("false")) multiplexer_1 (
    .in0(Num_A[15]), .in1(Num_B[15]), .out(Sum[15]), .sel(comparator_1_num_a___num_b));
  Extender extender_1 (.Exponent(Num_A[14:11]), .Fraction(Num_A[10:0]), .Significand(extender_1_significand));
  Multiplexer #(.width(4), .disabled(0), .enable("false")) multiplexer_2 (
    .in0(Num_A[14:11]), .in1(Num_B[14:11]), .out(multiplexer_2_out), .sel(comparator_1_num_a___num_b));
  xor xor_1 (xor_1_out, Num_A[15], Num_B[15]);
  Comparator comparator_1 (
    .Fraction_A(Num_A[10:0]), .Exponent_A(Num_A[14:11]), .Fraction_B(Num_B[10:0]), .Exponent_B(Num_B[14:11]),
    .Exponent_Diff(comparator_1_exponent_diff), .Num_A___Num_B(comparator_1_num_a___num_b));
  Normalizer normalizer_1 (
    .Significand_In(adder_1_out), .Fraction_Out(Sum[10:0]), .Underflow(Underflow), .Overflow(Overflow),
    .Exponent_In(multiplexer_2_out), .Exponent_Out(Sum[14:11]));
  Multiplexer #(.width(13), .disabled(0), .enable("false")) multiplexer_3 (
    .in0(extender_1_significand), .in1(extender_2_significand), .out(multiplexer_3_out),
    .sel(comparator_1_num_a___num_b));
  Extender extender_2 (.Exponent(Num_B[14:11]), .Fraction(Num_B[10:0]), .Significand(extender_2_significand));
  Multiplexer #(.width(13), .disabled(0), .enable("false")) multiplexer_4 (
    .in0(extender_2_significand), .in1(extender_1_significand), .out(multiplexer_4_out),
    .sel(comparator_1_num_a___num_b));
  Shifter #(.width(13), .shift("lr")) shifter_1 (
    .in(multiplexer_4_out), .\dist (comparator_1_exponent_diff), .out(shifter_1_out));
  Negator negator_1 (.Subtract(xor_1_out), .Significand_in(shifter_1_out), .Significand_out(negator_1_significand_out));
  Adder #(.width(13)) adder_1 (
    .a(negator_1_significand_out), .b(multiplexer_3_out), .out(adder_1_out), .cin(1'b0));  // open: cout

  // Notes on the sheet:
  //   larger exp
  //   larger sig
  //   smaller sig
endmodule

module Comparator (
  input  [3:0] Exponent_B,
  input  [3:0] Exponent_A,
  input  [10:0] Fraction_A,
  input  [10:0] Fraction_B,
  output [3:0] Exponent_Diff,
  output Num_A___Num_B
);

  wire subtractor_1_bout;
  wire [3:0] negator_1_out, subtractor_1_out;

  Subtractor #(.width(4)) subtractor_1 (
    .a(Exponent_A), .b(Exponent_B), .out(subtractor_1_out), .bin(1'b0), .bout(subtractor_1_bout));
  Comparator_part #(.width(15), .mode("unsigned")) comparator_1 (
    .a({Exponent_A, Fraction_A}), .b({Exponent_B, Fraction_B}), .lt(Num_A___Num_B));  // open: gt, eq
  Negator_part #(.width(4)) negator_1 (.in(subtractor_1_out), .out(negator_1_out));
  Multiplexer #(.width(4), .disabled(0), .enable("false")) multiplexer_1 (
    .in0(subtractor_1_out), .in1(negator_1_out), .out(Exponent_Diff), .sel(subtractor_1_bout));
endmodule

module Extender (
  input  [3:0] Exponent,
  input  [10:0] Fraction,
  output [12:0] Significand
);

  or or_1 (Significand[11], Exponent[3], Exponent[2], Exponent[1], Exponent[0]);

  assign {Significand[12], Significand[10:0]} = {1'b0, Fraction};
endmodule
