// Logisim project Pipelined 8 bit MIPS.circ as structural Verilog: 9 circuits, main circuit main
module main (
  output [7:0] out_1,
  output [7:0] out_2
);

  wire clock_1_out, control_unit_1_regwrite, ex_mem_1_out_5, id_ex_1_out_9, mem_wb_1_out_5;
  wire [1:0] Forwarding_Unit_forward_a, Forwarding_Unit_forward_b;
  wire [2:0] control_unit_1_aluop, id_ex_1_out_10;
  wire [3:0] ex_mem_1_out_6, id_ex_1_out_11, id_ex_1_out_12, id_ex_1_out_13, mem_wb_1_out_6;
  wire [7:0] adder_1_out, ex_mem_1_out_7, id_ex_1_out_14, id_ex_1_out_15, multiplexer_1_out,
       multiplexer_2_out, PC_q, register_file_1_readdata1, register_file_1_readdata2;
  wire [19:0] if_id_1_out_3, rom_1_data;

  Clock clock_1 (.out(clock_1_out));
  Register PC (.D(adder_1_out), .Q(PC_q), .clk(clock_1_out));  // open: en, clr
  Adder adder_1 (.a(PC_q), .b(8'h1), .out(adder_1_out), .cin(1'b0));  // open: cout
  ROM #(.dataWidth(20)) rom_1 (.addr(PC_q), .data(rom_1_data));  // open: sel
  IF_ID if_id_1 (.in_1(rom_1_data), .in_2(clock_1_out), .out_3(if_id_1_out_3));
  Control_Unit control_unit_1 (
    .Opcode(if_id_1_out_3[19:16]), .RegWrite(control_unit_1_regwrite), .ALUop(control_unit_1_aluop));  // open: MemRead, MemWrite, MemtoReg, RegDst, ALUSrc1, ALUSrc2, branch_equal, branch_not_equal, jump
  Register_File register_file_1 (
    .WriteData(out_2), .ReadRegister1(if_id_1_out_3[15:12]), .RegWrite(mem_wb_1_out_5),
    .WriteRegister(mem_wb_1_out_6), .ReadRegister2(if_id_1_out_3[11:8]), .Clock(clock_1_out),
    .ReadData1(register_file_1_readdata1), .ReadData2(register_file_1_readdata2));
  ID_EX id_ex_1 (
    .in_1(control_unit_1_regwrite), .in_2(control_unit_1_aluop), .in_3(if_id_1_out_3[15:12]),
    .in_4(if_id_1_out_3[11:8]), .in_5(if_id_1_out_3[7:4]), .in_6(register_file_1_readdata1),
    .in_7(register_file_1_readdata2), .in_8(clock_1_out), .out_9(id_ex_1_out_9), .out_10(id_ex_1_out_10),
    .out_11(id_ex_1_out_11), .out_12(id_ex_1_out_12), .out_13(id_ex_1_out_13), .out_14(id_ex_1_out_14),
    .out_15(id_ex_1_out_15));
  Multiplexer #(.select(2), .width(8), .enable("false")) multiplexer_1 (
    .in0(id_ex_1_out_14), .in1(out_2), .in2(ex_mem_1_out_7), .out(multiplexer_1_out),
    .sel(Forwarding_Unit_forward_a));  // open: in3
  Multiplexer #(.select(2), .width(8), .enable("false")) multiplexer_2 (
    .in0(id_ex_1_out_15), .in1(out_2), .in2(ex_mem_1_out_7), .out(multiplexer_2_out),
    .sel(Forwarding_Unit_forward_b));  // open: in3
  ALU alu_1 (.A(multiplexer_1_out), .B(multiplexer_2_out), .ALUop(id_ex_1_out_10), .F(out_1));  // open: ZF
  Forwarding_Unit Forwarding_Unit (
    .EX_MEM_RegWrite(ex_mem_1_out_5), .MEM_WB_RegWrite(mem_wb_1_out_5), .EX_MEM_Rd(ex_mem_1_out_6),
    .MEM_WB_Rd(mem_wb_1_out_6), .ID_EX_Rs(id_ex_1_out_11), .ID_EX_Rt(id_ex_1_out_12),
    .Forward_A(Forwarding_Unit_forward_a), .Forward_B(Forwarding_Unit_forward_b));
  EX_MEM ex_mem_1 (
    .in_1(id_ex_1_out_9), .in_2(id_ex_1_out_13), .in_3(out_1), .in_4(clock_1_out), .out_5(ex_mem_1_out_5),
    .out_6(ex_mem_1_out_6), .out_7(ex_mem_1_out_7));
  MEM_WB mem_wb_1 (
    .in_1(ex_mem_1_out_5), .in_2(ex_mem_1_out_6), .in_3(ex_mem_1_out_7), .in_4(clock_1_out),
    .out_5(mem_wb_1_out_5), .out_6(mem_wb_1_out_6), .out_7(out_2));
  RAM #(.bus("separate")) ram_1 ();  // open: addr, din, data, str, sel, clk, ld, clr

  // Notes on the sheet:
  //   Instruction Memory
  //   contents of rom_1 (hex, n*v repeats v):
  //   43420 22350 2450 45450
  //   IF/ID
  //   Control_Unit
  //   Registers_File
  //   ID/EX
  //   ALU
  //   EX/MEM
  //   Data Memory
  //   MEM/WB
endmodule

module ALU (
  input  [7:0] A,
  input  [7:0] B,
  input  [2:0] ALUop,
  output ZF,
  output [7:0] F
);

  wire [7:0] adder_1_out, and_1_out, nor_1_out, or_1_out, subtractor_1_out;
  wire [15:0] shifter_1_out, shifter_2_out;

  Adder adder_1 (.a(A), .b(B), .out(adder_1_out), .cin(1'b0));  // open: cout
  Subtractor subtractor_1 (.a(A), .b(B), .out(subtractor_1_out), .bin(1'b0));  // open: bout
  assign or_1_out = A | B;  // OR_Gate or_1, 8 bits wide
  assign and_1_out = A & B;  // AND_Gate and_1, 8 bits wide
  assign nor_1_out = ~(A | B);  // NOR_Gate nor_1, 8 bits wide
  Shifter #(.width(16)) shifter_1 (.in({{8{1'b0}}, A}), .\dist (B[3:0]), .out(shifter_1_out));
  Shifter #(.width(16), .shift("lr")) shifter_2 (.in({{8{1'b0}}, A}), .\dist (B[3:0]), .out(shifter_2_out));
  Multiplexer #(.select(3), .width(8), .enable("false")) multiplexer_1 (
    .in0(adder_1_out), .in1(subtractor_1_out), .in2(or_1_out), .in3(and_1_out), .in4(nor_1_out),
    .in5(shifter_1_out[7:0]), .in6(shifter_2_out[7:0]), .in7({8{1'b0}}), .out(F), .sel(ALUop));
  nor nor_2 (ZF, F[0], F[1], F[2], F[3], F[4], F[5], F[6], F[7]);
endmodule

module Register_File (
  input  [7:0] WriteData,
  input  [3:0] ReadRegister1,
  input  RegWrite,
  input  [3:0] WriteRegister,
  input  Clock,
  input  [3:0] ReadRegister2,
  output [7:0] ReadData1,
  output [7:0] ReadData2
);

  wire decoder_1_out0, decoder_1_out1, decoder_1_out2, decoder_1_out3, decoder_1_out4, decoder_1_out5,
       decoder_1_out6, decoder_1_out7;
  wire [7:0] sp_q, t0_q, t1_q, t2_q, t3_q, t4_q, zero_q;

  Decoder #(.select(3), .disabled(0)) decoder_1 (
    .out0(decoder_1_out0), .out1(decoder_1_out1), .out2(decoder_1_out2), .out3(decoder_1_out3),
    .out4(decoder_1_out4), .out5(decoder_1_out5), .out6(decoder_1_out6), .out7(decoder_1_out7),
    .sel(WriteRegister[2:0]), .en(RegWrite));
  Register #(.trigger("falling")) zero (.D(WriteData), .en(decoder_1_out0), .Q(zero_q), .clk(Clock));  // open: clr
  Register #(.trigger("falling")) t0 (.D(WriteData), .en(decoder_1_out1), .Q(t0_q), .clk(Clock));  // open: clr
  Register #(.trigger("falling")) t1 (.D(WriteData), .en(decoder_1_out2), .Q(t1_q), .clk(Clock));  // open: clr
  Register #(.trigger("falling")) t2 (.D(WriteData), .en(decoder_1_out3), .Q(t2_q), .clk(Clock));  // open: clr
  Register #(.trigger("falling")) t3 (.D(WriteData), .en(decoder_1_out4), .Q(t3_q), .clk(Clock));  // open: clr
  Register #(.trigger("falling")) t4 (.D(WriteData), .en(decoder_1_out5), .Q(t4_q), .clk(Clock));  // open: clr
  Register #(.trigger("falling")) sp (.D(WriteData), .en(decoder_1_out6), .Q(sp_q), .clk(Clock));  // open: clr
  Multiplexer #(.select(3), .width(8), .enable("false")) multiplexer_1 (
    .in0(zero_q), .in1(t0_q), .in2(t1_q), .in3(t2_q), .in4(t3_q), .in5(t4_q), .in6(sp_q), .in7({8{1'b0}}),
    .out(ReadData1), .sel(ReadRegister1[2:0]));
  Multiplexer #(.select(3), .width(8), .enable("false")) multiplexer_2 (
    .in0(zero_q), .in1(t0_q), .in2(t1_q), .in3(t2_q), .in4(t3_q), .in5(t4_q), .in6(sp_q), .in7({8{1'b0}}),
    .out(ReadData2), .sel(ReadRegister2[2:0]));
endmodule

module Control_Unit (
  input  [3:0] Opcode,
  output RegWrite,
  output MemRead,
  output MemWrite,
  output MemtoReg,
  output RegDst,
  output ALUSrc1,
  output [1:0] ALUSrc2,
  output [2:0] ALUop,
  output branch_equal,
  output branch_not_equal,
  output jump
);

  wire [15:14] rom_1_data;

  ROM #(.addrWidth(4), .dataWidth(16)) rom_1 (
    .addr(Opcode),
    .data({rom_1_data, jump, branch_not_equal, branch_equal, ALUop, ALUSrc2, ALUSrc1, RegDst, MemtoReg, MemWrite, MemRead, RegWrite}));  // open: sel

  // Notes on the sheet:
  //   contents of rom_1 (hex, n*v repeats v):
  //   211 281 111 571 11 381 311 81 671 411 181 2700 84 900 1100 8b
endmodule

module Forwarding_Unit (
  input  EX_MEM_RegWrite,
  input  MEM_WB_RegWrite,
  input  [3:0] EX_MEM_Rd,
  input  [3:0] MEM_WB_Rd,
  input  [3:0] ID_EX_Rs,
  input  [3:0] ID_EX_Rt,
  output [1:0] Forward_A,
  output [1:0] Forward_B
);

  wire comparator_1_eq, comparator_2_eq, comparator_3_eq, comparator_4_eq, not_1_out, not_2_out, or_1_out,
       or_2_out;

  or or_1 (or_1_out, EX_MEM_Rd[0], EX_MEM_Rd[1], EX_MEM_Rd[2], EX_MEM_Rd[3]);
  Comparator #(.width(4)) comparator_1 (.a(EX_MEM_Rd), .b(ID_EX_Rs), .eq(comparator_1_eq));  // open: gt, lt
  Comparator #(.width(4)) comparator_2 (.a(EX_MEM_Rd), .b(ID_EX_Rt), .eq(comparator_2_eq));  // open: gt, lt
  and and_1 (Forward_A[1], EX_MEM_RegWrite, or_1_out, comparator_1_eq);
  and and_2 (Forward_B[1], EX_MEM_RegWrite, or_1_out, comparator_2_eq);
  Comparator #(.width(4)) comparator_3 (.a(MEM_WB_Rd), .b(ID_EX_Rs), .eq(comparator_3_eq));  // open: gt, lt
  Comparator #(.width(4)) comparator_4 (.a(MEM_WB_Rd), .b(ID_EX_Rt), .eq(comparator_4_eq));  // open: gt, lt
  or or_2 (or_2_out, MEM_WB_Rd[0], MEM_WB_Rd[1], MEM_WB_Rd[2], MEM_WB_Rd[3]);
  not not_1 (not_1_out, Forward_A[1]);
  not not_2 (not_2_out, Forward_B[1]);
  and and_3 (Forward_A[0], MEM_WB_RegWrite, or_2_out, not_1_out, comparator_3_eq);
  and and_4 (Forward_B[0], or_2_out, MEM_WB_RegWrite, not_2_out, comparator_4_eq);
endmodule

module IF_ID (
  input  [19:0] in_1,
  input  in_2,
  output [19:0] out_3
);

  Register #(.width(20)) Instruction (.D(in_1), .Q(out_3), .clk(in_2));  // open: en, clr
endmodule

module ID_EX (
  input  in_1,
  input  [2:0] in_2,
  input  [3:0] in_3,
  input  [3:0] in_4,
  input  [3:0] in_5,
  input  [7:0] in_6,
  input  [7:0] in_7,
  input  in_8,
  output out_9,
  output [2:0] out_10,
  output [3:0] out_11,
  output [3:0] out_12,
  output [3:0] out_13,
  output [7:0] out_14,
  output [7:0] out_15
);

  Register #(.width(1)) RegWrite (.D(in_1), .Q(out_9), .clk(in_8));  // open: en, clr
  Register #(.width(3)) AluOp (.D(in_2), .Q(out_10), .clk(in_8));  // open: en, clr
  Register #(.width(4)) Rs (.D(in_3), .Q(out_11), .clk(in_8));  // open: en, clr
  Register #(.width(4)) Rt (.D(in_4), .Q(out_12), .clk(in_8));  // open: en, clr
  Register #(.width(4)) Rd (.D(in_5), .Q(out_13), .clk(in_8));  // open: en, clr
  Register ReadData1 (.D(in_6), .Q(out_14), .clk(in_8));  // open: en, clr
  Register ReadData2 (.D(in_7), .Q(out_15), .clk(in_8));  // open: en, clr
endmodule

module EX_MEM (
  input  in_1,
  input  [3:0] in_2,
  input  [7:0] in_3,
  input  in_4,
  output out_5,
  output [3:0] out_6,
  output [7:0] out_7
);

  Register #(.width(1)) RegWrite (.D(in_1), .Q(out_5), .clk(in_4));  // open: en, clr
  Register #(.width(4)) WriteRegister (.D(in_2), .Q(out_6), .clk(in_4));  // open: en, clr
  Register Write_Data (.D(in_3), .Q(out_7), .clk(in_4));  // open: en, clr
endmodule

module MEM_WB (
  input  in_1,
  input  [3:0] in_2,
  input  [7:0] in_3,
  input  in_4,
  output out_5,
  output [3:0] out_6,
  output [7:0] out_7
);

  Register #(.width(1)) RegWrite (.D(in_1), .Q(out_5), .clk(in_4));  // open: en, clr
  Register #(.width(4)) WriteRegister (.D(in_2), .Q(out_6), .clk(in_4));  // open: en, clr
  Register Write_Data (.D(in_3), .Q(out_7), .clk(in_4));  // open: en, clr
endmodule
